# Fritzing sketch Layout (saved by Fritzing 0.9.3b)
circuit board: 8.46667cm x 5.64444cm
perfboards: 1

parts:
  WeMos_D1_Mini1 = WeMos D1 Mini
  R1 = Resistor [tolerance=±5% resistance=4.7k package=THT]
  DS1 = DS18B20 1-Wire Temperature Sensor Probe Cable

nets:
  3V3: WeMos_D1_Mini1.3V3, R1.Pin_0, DS1.VDD
  N1: WeMos_D1_Mini1.D2, R1.Pin_1, DS1.DQ
  N2: WeMos_D1_Mini1.G, DS1.GND
